// Digital circuit alu.dig as structural Verilog
module alu (
  input  [3:0] a,
  input  [3:0] b,
  input  [3:0] op,
  output [3:0] s,
  output C,
  output Z,
  output N
);

  wire add_c_out, soustracteur_1_c_out;
  wire [3:0] add_s, and_1_s, lsr_1_s, not_1_s, or_1_s, soustracteur_1_s, xor_1_s;

  add4bit add (.c_in(1'b0), .A(a), .B(b), .s(add_s), .c_out(add_c_out));
  soustracteur soustracteur_1 (.a(a), .b(b), .s(soustracteur_1_s), .c_out(soustracteur_1_c_out));
  \and  and_1 (.a(a), .b(b), .s(and_1_s));
  \or  or_1 (.a(a), .b(b), .s(or_1_s));
  \xor  xor_1 (.a(a), .b(b), .s(xor_1_s));
  lsr lsr_1 (.a(a), .s(lsr_1_s));  // open: c_out
  \not  not_1 (.a(a), .s(not_1_s));
  Multiplexer #(.Bits(4), .Selector_Bits(4)) multiplexer_1 (
    .sel(op), .in_0(add_s), .in_1(soustracteur_1_s), .in_2(and_1_s), .in_3(or_1_s), .in_4(xor_1_s),
    .in_5(lsr_1_s), .in_6(not_1_s), .in_7(b), .in_8(b), .in_9(b), .in_10(b), .in_11(b), .in_12(b), .in_13(b),
    .in_14(b), .in_15(b), .out(s));
  or or_2 (C, add_c_out, soustracteur_1_c_out);
  nor nor_1 (Z, s[0], s[1], s[2], s[3]);
  and and_2 (N, s[3], 1'b1);

  // Notes on the sheet:
  //   op: default 2
endmodule
